// Logisim project addRoundKey.circ as structural Verilog: 1 circuit, main circuit main
module main (
  input  e1,
  input  c1,
  input  e,
  input  c,
  input  e_2,
  input  c_2,
  input  e_3,
  input  c_3,
  input  e_4,
  input  c_4,
  input  e_5,
  input  c_5,
  input  e_6,
  input  c_6,
  input  e_7,
  input  c_7,
  output out_17,
  output out_18,
  output out_19,
  output out_20,
  output out_21,
  output out_22,
  output out_23,
  output out_24
);

  xor xor_1 (out_17, e1, c1);
  xor xor_2 (out_18, e, c);
  xor xor_3 (out_19, e_2, c_2);
  xor xor_4 (out_20, e_3, c_3);
  xor xor_5 (out_21, e_4, c_4);
  xor xor_6 (out_22, e_5, c_5);
  xor xor_7 (out_23, e_6, c_6);
  xor xor_8 (out_24, e_7, c_7);
endmodule
