// Logisim project rtl.circ as structural Verilog: 8 circuits, main circuit main
module main (
  input  [7:0] in_1,
  input  [7:0] in_2,
  input  [7:0] in_3,
  input  [7:0] in_4,
  input  [7:0] in_5,
  input  [7:0] in_6,
  input  [7:0] in_7,
  input  in_8,
  input  [7:0] in_9,
  input  [7:0] in_10,
  input  [7:0] in_11,
  input  [7:0] in_12,
  input  [7:0] in_13,
  input  [7:0] in_14,
  input  [7:0] in_15,
  input  in_16,
  input  [7:0] in_17,
  input  [7:0] in_18,
  input  [7:0] in_19,
  input  [7:0] in_20,
  input  [7:0] in_21,
  input  [7:0] in_22,
  input  [7:0] in_23,
  input  [7:0] in_24,
  input  [7:0] in_25,
  input  [7:0] in_26,
  input  [7:0] in_27,
  input  [7:0] in_28,
  input  [7:0] in_29,
  input  [7:0] in_30,
  input  [7:0] in_31,
  input  [7:0] in_32,
  input  [7:0] in_33,
  input  [7:0] in_34,
  input  [7:0] in_35,
  input  [7:0] in_36,
  input  [7:0] in_37,
  input  [7:0] in_38,
  input  [7:0] in_39,
  input  [7:0] in_40,
  input  [7:0] in_41,
  input  [7:0] in_42,
  input  [7:0] in_43,
  input  [7:0] in_44,
  input  [7:0] in_45,
  input  [7:0] in_46,
  input  [7:0] in_47,
  input  [7:0] in_48,
  input  [7:0] in_49,
  input  [7:0] in_50,
  input  [7:0] in_51,
  input  [7:0] in_52,
  input  [7:0] in_53,
  input  [7:0] in_54,
  input  [7:0] in_55,
  input  [7:0] in_56,
  input  [7:0] in_57,
  input  [7:0] in_58,
  input  [7:0] in_59,
  input  [7:0] in_60,
  input  [7:0] in_61,
  input  [7:0] in_62,
  input  [7:0] in_63,
  input  [7:0] in_64,
  input  [7:0] in_65,
  input  [7:0] in_66,
  input  [7:0] in_67,
  input  [7:0] in_68,
  input  [7:0] in_69
);

  wire clock_1_out;
  wire [7:0] adder_1_out, addroundkey_1_out_3, addroundkey_2_out_3, addroundkey_3_out_3, addroundkey_4_out_3,
       addroundkey_5_out_3, addroundkey_6_out_3, addroundkey_7_out_3, addroundkey_8_out_3,
       addroundkey_9_out_3, addroundkey_10_out_3, addroundkey_11_out_3, addroundkey_12_out_3,
       addroundkey_13_out_3, addroundkey_14_out_3, addroundkey_15_out_3, addroundkey_16_out_3, c_2_q, c_3_q,
       c_4_q, c_5_q, c_6_q, c_7_q, c_8_q, c_9_q, c_10_q, c_11_q, c_12_q, c_13_q, c_14_q, c_15_q, c_16_q, c_q,
       e_2_q, e_3_q, e_4_q, e_5_q, e_6_q, e_7_q, e_8_q, e_9_q, e_10_q, e_11_q, e_12_q, e_13_q, e_14_q,
       e_15_q, e_16_q, e_q, lastround_1_out_33, lastround_1_out_34, lastround_1_out_35, lastround_1_out_36,
       lastround_1_out_37, lastround_1_out_38, lastround_1_out_39, lastround_1_out_40, lastround_1_out_41,
       lastround_1_out_42, lastround_1_out_43, lastround_1_out_44, lastround_1_out_45, lastround_1_out_46,
       lastround_1_out_47, lastround_1_out_48, multiplexer_1_out, multiplexer_2_out, multiplexer_3_out,
       multiplexer_4_out, multiplexer_5_out, multiplexer_6_out, multiplexer_7_out, multiplexer_8_out,
       multiplexer_9_out, multiplexer_10_out, multiplexer_11_out, multiplexer_12_out, multiplexer_13_out,
       multiplexer_14_out, multiplexer_15_out, multiplexer_16_out, register_1_q, register_2_q, register_3_q,
       register_4_q, register_5_q, register_6_q, register_8_q, register_9_q, register_10_q, register_11_q,
       register_12_q, register_13_q, register_14_q, register_15_q, register_16_q, register_17_q,
       register_18_q, register_19_q, register_20_q, register_21_q, register_22_q, register_23_q,
       register_24_q, register_25_q, register_26_q, register_27_q, register_28_q, register_29_q,
       register_30_q, register_31_q, register_32_q, register_33_q, register_34_q, register_35_q,
       round_1_out_33, round_1_out_34, round_1_out_35, round_1_out_36, round_1_out_37, round_1_out_38,
       round_1_out_39, round_1_out_40, round_1_out_41, round_1_out_42, round_1_out_43, round_1_out_44,
       round_1_out_45, round_1_out_46, round_1_out_47, round_1_out_48;

  Clock clock_1 (.out(clock_1_out));
  Register register_1 (.D(register_2_q), .Q(register_1_q), .clk(clock_1_out));  // open: en, clr
  Adder adder_1 (.a(register_1_q), .b(in_5), .out(adder_1_out));  // open: cin, cout
  Register e (.D(in_36), .Q(e_q));  // open: en, clk, clr
  Register c (.D(in_39), .Q(c_q));  // open: en, clk, clr
  Register e_2 (.D(in_40), .Q(e_2_q));  // open: en, clk, clr
  Register c_2 (.D(in_41), .Q(c_2_q));  // open: en, clk, clr
  Register e_3 (.D(in_42), .Q(e_3_q));  // open: en, clk, clr
  Register c_3 (.D(in_43), .Q(c_3_q));  // open: en, clk, clr
  Register e_4 (.D(in_44), .Q(e_4_q));  // open: en, clk, clr
  Register c_4 (.D(in_45), .Q(c_4_q));  // open: en, clk, clr
  Register e_5 (.D(in_46), .Q(e_5_q));  // open: en, clk, clr
  Register c_5 (.D(in_47), .Q(c_5_q));  // open: en, clk, clr
  Register e_6 (.D(in_48), .Q(e_6_q));  // open: en, clk, clr
  Register c_6 (.D(in_49), .Q(c_6_q));  // open: en, clk, clr
  Register e_7 (.D(in_50), .Q(e_7_q));  // open: en, clk, clr
  Register c_7 (.D(in_51), .Q(c_7_q));  // open: en, clk, clr
  Register e_8 (.D(in_52), .Q(e_8_q));  // open: en, clk, clr
  Register c_8 (.D(in_53), .Q(c_8_q));  // open: en, clk, clr
  Register e_9 (.D(in_54), .Q(e_9_q));  // open: en, clk, clr
  Register c_9 (.D(in_55), .Q(c_9_q));  // open: en, clk, clr
  Register e_10 (.D(in_56), .Q(e_10_q));  // open: en, clk, clr
  Register c_10 (.D(in_57), .Q(c_10_q));  // open: en, clk, clr
  Register e_11 (.D(in_58), .Q(e_11_q));  // open: en, clk, clr
  Register c_11 (.D(in_59), .Q(c_11_q));  // open: en, clk, clr
  Register e_12 (.D(in_60), .Q(e_12_q));  // open: en, clk, clr
  Register c_12 (.D(in_61), .Q(c_12_q));  // open: en, clk, clr
  Register e_13 (.D(in_62), .Q(e_13_q));  // open: en, clk, clr
  Register c_13 (.D(in_63), .Q(c_13_q));  // open: en, clk, clr
  Register e_14 (.D(in_64), .Q(e_14_q));  // open: en, clk, clr
  Register c_14 (.D(in_65), .Q(c_14_q));  // open: en, clk, clr
  Register e_15 (.D(in_66), .Q(e_15_q));  // open: en, clk, clr
  Register c_15 (.D(in_67), .Q(c_15_q));  // open: en, clk, clr
  Register e_16 (.D(in_68), .Q(e_16_q));  // open: en, clk, clr
  Register c_16 (.D(in_69), .Q(c_16_q));  // open: en, clk, clr
  Register register_2 (.D(adder_1_out), .Q(register_2_q), .clk(clock_1_out));  // open: en, clr
  addRoundKey addroundkey_1 (.in_1(e_q), .in_2(c_q), .out_3(addroundkey_1_out_3));
  addRoundKey addroundkey_2 (.in_1(e_2_q), .in_2(c_2_q), .out_3(addroundkey_2_out_3));
  addRoundKey addroundkey_3 (.in_1(e_3_q), .in_2(c_3_q), .out_3(addroundkey_3_out_3));
  addRoundKey addroundkey_4 (.in_1(e_4_q), .in_2(c_4_q), .out_3(addroundkey_4_out_3));
  addRoundKey addroundkey_5 (.in_1(e_5_q), .in_2(c_5_q), .out_3(addroundkey_5_out_3));
  addRoundKey addroundkey_6 (.in_1(e_6_q), .in_2(c_6_q), .out_3(addroundkey_6_out_3));
  addRoundKey addroundkey_7 (.in_1(e_7_q), .in_2(c_7_q), .out_3(addroundkey_7_out_3));
  addRoundKey addroundkey_8 (.in_1(e_8_q), .in_2(c_8_q), .out_3(addroundkey_8_out_3));
  addRoundKey addroundkey_9 (.in_1(e_9_q), .in_2(c_9_q), .out_3(addroundkey_9_out_3));
  addRoundKey addroundkey_10 (.in_1(e_10_q), .in_2(c_10_q), .out_3(addroundkey_10_out_3));
  addRoundKey addroundkey_11 (.in_1(e_11_q), .in_2(c_11_q), .out_3(addroundkey_11_out_3));
  addRoundKey addroundkey_12 (.in_1(e_12_q), .in_2(c_12_q), .out_3(addroundkey_12_out_3));
  addRoundKey addroundkey_13 (.in_1(e_13_q), .in_2(c_13_q), .out_3(addroundkey_13_out_3));
  addRoundKey addroundkey_14 (.in_1(e_14_q), .in_2(c_14_q), .out_3(addroundkey_14_out_3));
  addRoundKey addroundkey_15 (.in_1(e_15_q), .in_2(c_15_q), .out_3(addroundkey_15_out_3));
  addRoundKey addroundkey_16 (.in_1(e_16_q), .in_2(c_16_q), .out_3(addroundkey_16_out_3));
  Register register_3 (.D(multiplexer_1_out), .Q(register_3_q));  // open: en, clk, clr
  Multiplexer #(.width(8), .enable("false")) multiplexer_1 (
    .in0(round_1_out_33), .in1(addroundkey_1_out_3), .out(multiplexer_1_out), .sel(in_16));
  Multiplexer #(.width(8)) multiplexer_2 (
    .in0(round_1_out_34), .in1(addroundkey_2_out_3), .out(multiplexer_2_out), .sel(in_16));  // open: en
  Multiplexer #(.width(8)) multiplexer_3 (
    .in0(round_1_out_35), .in1(addroundkey_3_out_3), .out(multiplexer_3_out), .sel(in_16));  // open: en
  Register register_4 (.D(multiplexer_3_out), .Q(register_4_q));  // open: en, clk, clr
  Register register_5 (.D(multiplexer_4_out), .Q(register_5_q));  // open: en, clk, clr
  Multiplexer #(.width(8)) multiplexer_4 (
    .in0(round_1_out_36), .in1(addroundkey_4_out_3), .out(multiplexer_4_out), .sel(in_16));  // open: en
  Multiplexer #(.width(8)) multiplexer_5 (
    .in0(round_1_out_37), .in1(addroundkey_5_out_3), .out(multiplexer_5_out), .sel(in_16));  // open: en
  Register register_6 (.D(multiplexer_5_out), .Q(register_6_q));  // open: en, clk, clr
  Multiplexer #(.width(8)) multiplexer_6 (
    .in0(round_1_out_38), .in1(addroundkey_6_out_3), .out(multiplexer_6_out), .sel(in_16));  // open: en
  Multiplexer #(.width(8)) multiplexer_7 (
    .in0(round_1_out_39), .in1(addroundkey_7_out_3), .out(multiplexer_7_out), .sel(in_16));  // open: en
  Multiplexer #(.width(8)) multiplexer_8 (
    .in0(round_1_out_40), .in1(addroundkey_8_out_3), .out(multiplexer_8_out), .sel(in_16));  // open: en
  Multiplexer #(.width(8)) multiplexer_9 (
    .in0(round_1_out_41), .in1(addroundkey_9_out_3), .out(multiplexer_9_out), .sel(in_16));  // open: en
  Multiplexer #(.width(8)) multiplexer_10 (
    .in0(round_1_out_42), .in1(addroundkey_10_out_3), .out(multiplexer_10_out), .sel(in_16));  // open: en
  Multiplexer #(.width(8)) multiplexer_11 (
    .in0(round_1_out_43), .in1(addroundkey_11_out_3), .out(multiplexer_11_out), .sel(in_16));  // open: en
  Multiplexer #(.width(8)) multiplexer_12 (
    .in0(round_1_out_44), .in1(addroundkey_12_out_3), .out(multiplexer_12_out), .sel(in_16));  // open: en
  Multiplexer #(.width(8)) multiplexer_13 (
    .in0(round_1_out_45), .in1(addroundkey_13_out_3), .out(multiplexer_13_out), .sel(in_16));  // open: en
  Multiplexer #(.width(8)) multiplexer_14 (
    .in0(round_1_out_46), .in1(addroundkey_14_out_3), .out(multiplexer_14_out), .sel(in_16));  // open: en
  Multiplexer #(.width(8)) multiplexer_15 (
    .in0(round_1_out_47), .in1(addroundkey_15_out_3), .out(multiplexer_15_out), .sel(in_16));  // open: en
  Multiplexer #(.width(8)) multiplexer_16 (
    .in0(round_1_out_48), .in1(addroundkey_16_out_3), .out(multiplexer_16_out), .sel(in_16));  // open: en
  Register register_7 ();  // open: D, en, Q, clk, clr
  Comparator comparator_1 (.a(register_2_q), .b(in_17), .eq(in_16));  // open: gt, lt
  Register register_8 (.D(multiplexer_2_out), .Q(register_8_q));  // open: en, clk, clr
  Register register_9 (.D(multiplexer_6_out), .Q(register_9_q));  // open: en, clk, clr
  Register register_10 (.D(multiplexer_7_out), .Q(register_10_q));  // open: en, clk, clr
  Register register_11 (.D(multiplexer_8_out), .Q(register_11_q));  // open: en, clk, clr
  Register register_12 (.D(multiplexer_9_out), .Q(register_12_q));  // open: en, clk, clr
  Register register_13 (.D(multiplexer_10_out), .Q(register_13_q));  // open: en, clk, clr
  Register register_14 (.D(multiplexer_11_out), .Q(register_14_q));  // open: en, clk, clr
  Register register_15 (.D(multiplexer_16_out), .Q(register_15_q));  // open: en, clk, clr
  Comparator comparator_2 (.a(register_2_q), .b(in_9), .eq(in_8));  // open: gt, lt
  Register register_16 (.D(multiplexer_12_out), .Q(register_16_q));  // open: en, clk, clr
  Register register_17 (.D(multiplexer_13_out), .Q(register_17_q));  // open: en, clk, clr
  Register register_18 (.D(multiplexer_14_out), .Q(register_18_q));  // open: en, clk, clr
  Register register_19 (.D(multiplexer_15_out), .Q(register_19_q));  // open: en, clk, clr
  round round_1 (
    .in_1(register_3_q), .chave(in_37), .in_2(register_8_q), .chave_2(in_34), .chave_3(in_32),
    .in_3(register_4_q), .chave_4(in_30), .in_4(register_5_q), .in_6(register_6_q), .in_21(in_28),
    .in_7(register_9_q), .in_22(in_26), .in_23(in_24), .in_8(register_10_q), .in_24(in_22),
    .in_9(register_11_q), .in_25(in_20), .in_11(register_12_q), .in_26(in_18), .in_27(in_14),
    .in_12(register_13_q), .in_28(in_12), .in_13(register_14_q), .in_29(in_10), .in_30(in_6),
    .in_14(register_16_q), .in_31(in_3), .in_16(register_17_q), .in_32(in_1), .in_17(register_18_q),
    .in_18(register_19_q), .in_19(register_15_q), .out_33(round_1_out_33), .out_34(round_1_out_34),
    .out_35(round_1_out_35), .out_36(round_1_out_36), .out_37(round_1_out_37), .out_38(round_1_out_38),
    .out_39(round_1_out_39), .out_40(round_1_out_40), .out_41(round_1_out_41), .out_42(round_1_out_42),
    .out_43(round_1_out_43), .out_44(round_1_out_44), .out_45(round_1_out_45), .out_46(round_1_out_46),
    .out_47(round_1_out_47), .out_48(round_1_out_48));
  Register register_20 (.D(round_1_out_33), .Q(register_20_q), .clk(in_8));  // open: en, clr
  Register register_21 (.D(round_1_out_34), .Q(register_21_q), .clk(in_8));  // open: en, clr
  Register register_22 (.D(round_1_out_35), .Q(register_22_q), .clk(in_8));  // open: en, clr
  Register register_23 (.D(round_1_out_36), .Q(register_23_q), .clk(in_8));  // open: en, clr
  Register register_24 (.D(round_1_out_37), .Q(register_24_q), .clk(in_8));  // open: en, clr
  Register register_25 (.D(round_1_out_38), .Q(register_25_q), .clk(in_8));  // open: en, clr
  Register register_26 (.D(round_1_out_39), .Q(register_26_q), .clk(in_8));  // open: en, clr
  Register register_27 (.D(round_1_out_40), .Q(register_27_q), .clk(in_8));  // open: en, clr
  Register register_28 (.D(round_1_out_41), .Q(register_28_q), .clk(in_8));  // open: en, clr
  Register register_29 (.D(round_1_out_42), .Q(register_29_q), .clk(in_8));  // open: en, clr
  Register register_30 (.D(round_1_out_43), .Q(register_30_q), .clk(in_8));  // open: en, clr
  Register register_31 (.D(round_1_out_44), .Q(register_31_q), .clk(in_8));  // open: en, clr
  Register register_32 (.D(round_1_out_45), .Q(register_32_q), .clk(in_8));  // open: en, clr
  Register register_33 (.D(round_1_out_46), .Q(register_33_q), .clk(in_8));  // open: en, clr
  Register register_34 (.D(round_1_out_47), .Q(register_34_q), .clk(in_8));  // open: en, clr
  Register register_35 (.D(round_1_out_48), .Q(register_35_q), .clk(in_8));  // open: en, clr
  lastRound lastround_1 (
    .in_1(register_20_q), .chave(in_38), .in_3(register_21_q), .chave_2(in_35), .in_5(register_22_q),
    .chave_3(in_33), .in_7(register_23_q), .chave_4(in_31), .in_9(register_24_q), .chave_5(in_29),
    .in_11(register_25_q), .chave_6(in_27), .chave_7(in_25), .in_14(register_26_q), .chave_8(in_23),
    .in_16(register_27_q), .in_17(register_28_q), .in_18(register_29_q), .chave_9(in_21), .chave_10(in_19),
    .in_21(register_30_q), .chave_11(in_15), .chave_12(in_13), .in_24(register_31_q), .in_25(register_32_q),
    .in_26(register_33_q), .chave_13(in_11), .chave_14(in_7), .in_29(register_34_q), .chave_15(in_4),
    .chave_16(in_2), .in_32(register_35_q), .out_33(lastround_1_out_33), .out_34(lastround_1_out_34),
    .out_35(lastround_1_out_35), .out_36(lastround_1_out_36), .out_37(lastround_1_out_37),
    .out_38(lastround_1_out_38), .out_39(lastround_1_out_39), .out_40(lastround_1_out_40),
    .out_41(lastround_1_out_41), .out_42(lastround_1_out_42), .out_43(lastround_1_out_43),
    .out_44(lastround_1_out_44), .out_45(lastround_1_out_45), .out_46(lastround_1_out_46),
    .out_47(lastround_1_out_47), .out_48(lastround_1_out_48));
  Register register_36 (.D(lastround_1_out_33));  // open: en, Q, clk, clr
  Register register_37 (.D(lastround_1_out_34));  // open: en, Q, clk, clr
  Register register_38 (.D(lastround_1_out_35));  // open: en, Q, clk, clr
  Register register_39 (.D(lastround_1_out_36));  // open: en, Q, clk, clr
  Register register_40 (.D(lastround_1_out_37));  // open: en, Q, clk, clr
  Register register_41 (.D(lastround_1_out_38));  // open: en, Q, clk, clr
  Register register_42 (.D(lastround_1_out_39));  // open: en, Q, clk, clr
  Register register_43 (.D(lastround_1_out_40));  // open: en, Q, clk, clr
  Register register_44 (.D(lastround_1_out_41));  // open: en, Q, clk, clr
  Register register_45 (.D(lastround_1_out_42));  // open: en, Q, clk, clr
  Register register_46 (.D(lastround_1_out_43));  // open: en, Q, clk, clr
  Register register_47 (.D(lastround_1_out_44));  // open: en, Q, clk, clr
  Register register_48 (.D(lastround_1_out_45));  // open: en, Q, clk, clr
  Register register_49 (.D(lastround_1_out_46));  // open: en, Q, clk, clr
  Register register_50 (.D(lastround_1_out_47));  // open: en, Q, clk, clr
  Register register_51 (.D(lastround_1_out_48));  // open: en, Q, clk, clr

  // Notes on the sheet:
  //   1º addRoundKey
  //   1º addRoundKey
  //   1º addRoundKey
  //   1º addRoundKey
  //   1º addRoundKey
  //   1º addRoundKey
  //   1º addRoundKey
  //   1º addRoundKey
  //   1º addRoundKey
  //   1º addRoundKey
  //   1º addRoundKey
  //   1º addRoundKey
  //   1º addRoundKey
  //   1º addRoundKey
  //   1º addRoundKey
  //   1º addRoundKey
endmodule

module addRoundKey (
  input  [7:0] in_1,
  input  [7:0] in_2,
  output [7:0] out_3
);

  xor xor_1 (out_3[0], in_1[0], in_2[0]);
  xor xor_2 (out_3[1], in_1[1], in_2[1]);
  xor xor_3 (out_3[2], in_1[2], in_2[2]);
  xor xor_4 (out_3[3], in_1[3], in_2[3]);
  xor xor_5 (out_3[4], in_1[4], in_2[4]);
  xor xor_6 (out_3[5], in_1[5], in_2[5]);
  xor xor_7 (out_3[6], in_1[6], in_2[6]);
  xor xor_8 (out_3[7], in_1[7], in_2[7]);
endmodule

module shiftRows2 (
  input  [7:0] in_1,
  input  [7:0] in_2,
  input  [7:0] in_3,
  input  [7:0] in_4,
  output [7:0] out_5,
  output [7:0] out_6,
  output [7:0] out_7,
  output [7:0] out_8
);


  assign out_5 = in_2;
  assign out_6 = in_3;
  assign out_7 = in_4;
  assign out_8 = in_1;
endmodule

module shiftRows3 (
  input  [7:0] in_1,
  input  [7:0] in_2,
  input  [7:0] in_3,
  input  [7:0] in_4,
  output [7:0] out_5,
  output [7:0] out_6,
  output [7:0] out_7,
  output [7:0] out_8
);


  assign out_5 = in_3;
  assign out_6 = in_4;
  assign out_7 = in_1;
  assign out_8 = in_2;
endmodule

module shiftRows4 (
  input  [7:0] in_1,
  input  [7:0] in_2,
  input  [7:0] in_3,
  input  [7:0] in_4,
  output [7:0] out_5,
  output [7:0] out_6,
  output [7:0] out_7,
  output [7:0] out_8
);


  assign out_5 = in_4;
  assign out_6 = in_1;
  assign out_7 = in_2;
  assign out_8 = in_3;
endmodule

module mixColumns (
  input  [7:0] in_1,
  input  [7:0] in_2,
  input  [7:0] in_3,
  input  [7:0] in_4,
  output [7:0] coluna1,
  output [7:0] coluna2,
  output [7:0] coluna3,
  output [7:0] coluna4
);

  wire [7:0] shifter_1_out, shifter_2_out, shifter_3_out, shifter_4_out, shifter_5_out, shifter_6_out,
       shifter_7_out, shifter_8_out, xor_1_out, xor_2_out, xor_3_out, xor_4_out;

  Shifter shifter_1 (.in(in_2), .\dist (3'b010), .out(shifter_1_out));
  Shifter shifter_2 (.in(in_3), .\dist (3'b010), .out(shifter_2_out));
  Shifter shifter_3 (.in(in_3), .\dist (3'b010), .out(shifter_3_out));
  Shifter shifter_4 (.in(in_4), .\dist (3'b010), .out(shifter_4_out));
  Shifter shifter_5 (.in(in_1), .\dist (3'b010), .out(shifter_5_out));
  Shifter shifter_6 (.in(in_2), .\dist (3'b010), .out(shifter_6_out));
  Shifter shifter_7 (.in(in_1), .\dist (3'b010), .out(shifter_7_out));
  Shifter shifter_8 (.in(in_4), .\dist (3'b010), .out(shifter_8_out));
  assign xor_1_out = shifter_1_out ^ in_2;  // XOR_Gate xor_1, 8 bits wide
  assign xor_2_out = shifter_2_out ^ in_3;  // XOR_Gate xor_2, 8 bits wide
  assign xor_3_out = shifter_4_out ^ in_4;  // XOR_Gate xor_3, 8 bits wide
  assign xor_4_out = shifter_7_out ^ in_1;  // XOR_Gate xor_4, 8 bits wide
  ExactlyOne xor_5[7:0] (.out(coluna1), .in0(shifter_5_out), .in1(xor_1_out), .in2(in_3), .in3(in_4));
  ExactlyOne xor_6[7:0] (.out(coluna2), .in0(in_1), .in1(shifter_6_out), .in2(xor_2_out), .in3(in_4));
  ExactlyOne xor_7[7:0] (.out(coluna3), .in0(in_1), .in1(in_2), .in2(shifter_3_out), .in3(xor_3_out));
  ExactlyOne xor_8[7:0] (.out(coluna4), .in0(xor_4_out), .in1(in_2), .in2(in_3), .in3(shifter_8_out));
endmodule

module round (
  input  [7:0] in_1,
  input  [7:0] in_2,
  input  [7:0] in_3,
  input  [7:0] in_4,
  input  [7:0] chave,
  input  [7:0] in_6,
  input  [7:0] in_7,
  input  [7:0] in_8,
  input  [7:0] in_9,
  input  [7:0] chave_2,
  input  [7:0] in_11,
  input  [7:0] in_12,
  input  [7:0] in_13,
  input  [7:0] in_14,
  input  [7:0] chave_3,
  input  [7:0] in_16,
  input  [7:0] in_17,
  input  [7:0] in_18,
  input  [7:0] in_19,
  input  [7:0] chave_4,
  input  [7:0] in_21,
  input  [7:0] in_22,
  input  [7:0] in_23,
  input  [7:0] in_24,
  input  [7:0] in_25,
  input  [7:0] in_26,
  input  [7:0] in_27,
  input  [7:0] in_28,
  input  [7:0] in_29,
  input  [7:0] in_30,
  input  [7:0] in_31,
  input  [7:0] in_32,
  output [7:0] out_33,
  output [7:0] out_34,
  output [7:0] out_35,
  output [7:0] out_36,
  output [7:0] out_37,
  output [7:0] out_38,
  output [7:0] out_39,
  output [7:0] out_40,
  output [7:0] out_41,
  output [7:0] out_42,
  output [7:0] out_43,
  output [7:0] out_44,
  output [7:0] out_45,
  output [7:0] out_46,
  output [7:0] out_47,
  output [7:0] out_48
);

  wire [7:0] c_2_q, c_3_q, c_4_q, c_5_q, c_6_q, c_7_q, c_8_q, c_9_q, c_10_q, c_11_q, c_12_q, c_13_q, c_14_q,
       c_15_q, c_16_q, c_q, mixColumns1_coluna1, mixColumns1_coluna2, mixColumns1_coluna3,
       mixColumns1_coluna4, mixColumns2_coluna1, mixColumns2_coluna2, mixColumns2_coluna3,
       mixColumns2_coluna4, mixColumns3_coluna1, mixColumns3_coluna2, mixColumns3_coluna3,
       mixColumns3_coluna4, mixColumns4_coluna1, mixColumns4_coluna2, mixColumns4_coluna3,
       mixColumns4_coluna4, multiplexer_1_out, register_1_q, register_2_q, register_3_q, register_4_q,
       register_5_q, register_6_q, register_7_q, register_8_q, register_9_q, register_10_q, register_11_q,
       register_12_q, register_13_q, register_14_q, register_15_q, register_16_q, register_17_q,
       register_18_q, register_19_q, register_20_q, register_21_q, register_22_q, register_23_q,
       register_24_q, register_25_q, register_26_q, register_27_q, register_28_q, register_29_q,
       register_30_q, register_31_q, register_32_q, register_33_q, register_34_q, register_35_q,
       register_36_q, register_37_q, register_38_q, register_39_q, register_40_q, register_41_q,
       register_42_q, register_43_q, register_44_q, rom_1_data, rom_2_data, rom_3_data, rom_4_data,
       rom_5_data, rom_6_data, rom_7_data, rom_8_data, shiftrows2_1_out_5, shiftrows2_1_out_6,
       shiftrows2_1_out_7, shiftrows2_1_out_8, shiftrows3_1_out_5, shiftrows3_1_out_6, shiftrows3_1_out_7,
       shiftrows3_1_out_8, shiftrows4_1_out_5, shiftrows4_1_out_6, shiftrows4_1_out_7, shiftrows4_1_out_8,
       undriven, undriven_2, undriven_3, undriven_4, undriven_5;

  Multiplexer #(.select(4), .width(8)) multiplexer_1 (
    .in0(in_1), .in1(in_2), .in2(in_3), .in3(in_4), .in4(in_6), .in5(in_7), .in6(in_8), .in7(in_9),
    .in8(in_11), .in9(in_12), .in10(in_13), .in11(in_14), .in12(in_16), .in13(in_17), .in14(in_18),
    .in15(in_19), .out(multiplexer_1_out));  // open: sel, en
  ROM rom_1 (.addr(multiplexer_1_out), .data(rom_1_data));  // open: sel
  ROM rom_2 (.data(rom_2_data));  // open: addr, sel
  ROM rom_3 (.data(rom_3_data));  // open: addr, sel
  ROM rom_4 (.data(rom_4_data));  // open: addr, sel
  ROM rom_5 (.data(rom_5_data));  // open: addr, sel
  ROM rom_6 (.data(rom_6_data));  // open: addr, sel
  ROM rom_7 (.data(rom_7_data));  // open: addr, sel
  ROM rom_8 (.data(rom_8_data));  // open: addr, sel
  Register register_1 (.Q(register_1_q));  // open: D, en, clk, clr
  Register register_2 (.Q(register_2_q));  // open: D, en, clk, clr
  Register register_3 (.Q(register_3_q));  // open: D, en, clk, clr
  Register register_4 (.D(rom_1_data), .Q(register_4_q));  // open: en, clk, clr
  Register register_5 (.D(rom_2_data), .Q(register_5_q));  // open: en, clk, clr
  Register register_6 (.D(rom_3_data), .Q(register_6_q));  // open: en, clk, clr
  Register register_7 (.D(rom_4_data), .Q(register_7_q));  // open: en, clk, clr
  Register register_8 (.D(rom_5_data), .Q(register_8_q));  // open: en, clk, clr
  Register register_9 (.D(rom_6_data), .Q(register_9_q));  // open: en, clk, clr
  Register register_10 (.D(rom_7_data), .Q(register_10_q));  // open: en, clk, clr
  Register register_11 (.D(rom_8_data), .Q(register_11_q));  // open: en, clk, clr
  Register register_12 (.D(undriven_2), .Q(register_12_q));  // open: en, clk, clr
  Register register_13 (.D(undriven_3), .Q(register_13_q));  // open: en, clk, clr
  Register register_14 (.D(undriven_4), .Q(register_14_q));  // open: en, clk, clr
  Register register_15 (.D(undriven), .Q(register_15_q));  // open: en, clk, clr
  Register register_16 (.D(undriven_5), .Q(register_16_q));  // open: en, clk, clr
  shiftRows2 shiftrows2_1 (
    .in_1(register_8_q), .in_2(register_9_q), .in_3(register_10_q), .in_4(register_11_q),
    .out_5(shiftrows2_1_out_5), .out_6(shiftrows2_1_out_6), .out_7(shiftrows2_1_out_7),
    .out_8(shiftrows2_1_out_8));
  shiftRows3 shiftrows3_1 (
    .in_1(register_12_q), .in_2(register_13_q), .in_3(register_14_q), .in_4(register_1_q),
    .out_5(shiftrows3_1_out_5), .out_6(shiftrows3_1_out_6), .out_7(shiftrows3_1_out_7),
    .out_8(shiftrows3_1_out_8));
  shiftRows4 shiftrows4_1 (
    .in_1(register_2_q), .in_2(register_3_q), .in_3(register_15_q), .in_4(register_16_q),
    .out_5(shiftrows4_1_out_5), .out_6(shiftrows4_1_out_6), .out_7(shiftrows4_1_out_7),
    .out_8(shiftrows4_1_out_8));
  Register register_17 (.D(shiftrows3_1_out_5), .Q(register_17_q));  // open: en, clk, clr
  Register register_18 (.D(shiftrows3_1_out_6), .Q(register_18_q));  // open: en, clk, clr
  Register register_19 (.D(shiftrows3_1_out_7), .Q(register_19_q));  // open: en, clk, clr
  Register register_20 (.D(shiftrows3_1_out_8), .Q(register_20_q));  // open: en, clk, clr
  Register register_21 (.D(shiftrows4_1_out_5), .Q(register_21_q));  // open: en, clk, clr
  Register register_22 (.D(shiftrows4_1_out_6), .Q(register_22_q));  // open: en, clk, clr
  Register register_23 (.D(shiftrows4_1_out_7), .Q(register_23_q));  // open: en, clk, clr
  Register register_24 (.D(shiftrows4_1_out_8), .Q(register_24_q));  // open: en, clk, clr
  Register register_25 (.D(shiftrows2_1_out_5), .Q(register_25_q));  // open: en, clk, clr
  Register register_26 (.D(shiftrows2_1_out_6), .Q(register_26_q));  // open: en, clk, clr
  Register register_27 (.D(shiftrows2_1_out_7), .Q(register_27_q));  // open: en, clk, clr
  Register register_28 (.D(shiftrows2_1_out_8), .Q(register_28_q));  // open: en, clk, clr
  mixColumns mixColumns1 (
    .in_1(register_4_q), .in_2(register_25_q), .in_3(register_17_q), .in_4(register_21_q),
    .coluna1(mixColumns1_coluna1), .coluna2(mixColumns1_coluna2), .coluna3(mixColumns1_coluna3),
    .coluna4(mixColumns1_coluna4));
  mixColumns mixColumns2 (
    .in_1(register_5_q), .in_2(register_26_q), .in_3(register_18_q), .in_4(register_22_q),
    .coluna1(mixColumns2_coluna1), .coluna2(mixColumns2_coluna2), .coluna3(mixColumns2_coluna3),
    .coluna4(mixColumns2_coluna4));
  mixColumns mixColumns3 (
    .in_1(register_6_q), .in_2(register_27_q), .in_3(register_19_q), .in_4(register_23_q),
    .coluna1(mixColumns3_coluna1), .coluna2(mixColumns3_coluna2), .coluna3(mixColumns3_coluna3),
    .coluna4(mixColumns3_coluna4));
  mixColumns mixColumns4 (
    .in_1(register_7_q), .in_2(register_28_q), .in_3(register_20_q), .in_4(register_24_q),
    .coluna1(mixColumns4_coluna1), .coluna2(mixColumns4_coluna2), .coluna3(mixColumns4_coluna3),
    .coluna4(mixColumns4_coluna4));
  Register register_29 (.D(mixColumns1_coluna4), .Q(register_29_q));  // open: en, clk, clr
  Register c (.D(chave_4), .Q(c_q));  // open: en, clk, clr
  Register register_30 (.D(mixColumns2_coluna1), .Q(register_30_q));  // open: en, clk, clr
  Register register_31 (.D(mixColumns2_coluna2), .Q(register_31_q));  // open: en, clk, clr
  Register register_32 (.D(mixColumns2_coluna3), .Q(register_32_q));  // open: en, clk, clr
  Register register_33 (.D(mixColumns2_coluna4), .Q(register_33_q));  // open: en, clk, clr
  Register register_34 (.D(mixColumns4_coluna1), .Q(register_34_q));  // open: en, clk, clr
  Register c_2 (.D(in_29), .Q(c_2_q));  // open: en, clk, clr
  Register register_35 (.D(mixColumns4_coluna2), .Q(register_35_q));  // open: en, clk, clr
  Register c_3 (.D(in_30), .Q(c_3_q));  // open: en, clk, clr
  Register register_36 (.D(mixColumns4_coluna3), .Q(register_36_q));  // open: en, clk, clr
  Register c_4 (.D(in_31), .Q(c_4_q));  // open: en, clk, clr
  Register register_37 (.D(mixColumns4_coluna4), .Q(register_37_q));  // open: en, clk, clr
  Register c_5 (.D(in_32), .Q(c_5_q));  // open: en, clk, clr
  Register register_38 (.D(mixColumns1_coluna1), .Q(register_38_q));  // open: en, clk, clr
  Register c_6 (.D(chave), .Q(c_6_q));  // open: en, clk, clr
  Register register_39 (.D(mixColumns1_coluna2), .Q(register_39_q));  // open: en, clk, clr
  Register c_7 (.D(chave_2), .Q(c_7_q));  // open: en, clk, clr
  Register register_40 (.D(mixColumns1_coluna3), .Q(register_40_q));  // open: en, clk, clr
  Register c_8 (.D(chave_3), .Q(c_8_q));  // open: en, clk, clr
  addRoundKey addroundkey_1 (.in_1(register_29_q), .in_2(c_q), .out_3(out_36));
  Register c_9 (.D(in_21), .Q(c_9_q));  // open: en, clk, clr
  Register c_10 (.D(in_22), .Q(c_10_q));  // open: en, clk, clr
  Register c_11 (.D(in_23), .Q(c_11_q));  // open: en, clk, clr
  Register c_12 (.D(in_24), .Q(c_12_q));  // open: en, clk, clr
  addRoundKey addroundkey_2 (.in_1(register_34_q), .in_2(c_2_q), .out_3(out_45));
  addRoundKey addroundkey_3 (.in_1(register_35_q), .in_2(c_3_q), .out_3(out_46));
  addRoundKey addroundkey_4 (.in_1(register_36_q), .in_2(c_4_q), .out_3(out_47));
  addRoundKey addroundkey_5 (.in_1(register_37_q), .in_2(c_5_q), .out_3(out_48));
  addRoundKey addRoundKey_6 (.in_1(register_38_q), .in_2(c_6_q), .out_3(out_33));
  addRoundKey addroundkey_7 (.in_1(register_39_q), .in_2(c_7_q), .out_3(out_34));
  addRoundKey addroundkey_8 (.in_1(register_40_q), .in_2(c_8_q), .out_3(out_35));
  addRoundKey addroundkey_9 (.in_1(register_30_q), .in_2(c_9_q), .out_3(out_37));
  addRoundKey addroundkey_10 (.in_1(register_31_q), .in_2(c_10_q), .out_3(out_38));
  addRoundKey addroundkey_11 (.in_1(register_32_q), .in_2(c_11_q), .out_3(out_39));
  addRoundKey addroundkey_12 (.in_1(register_33_q), .in_2(c_12_q), .out_3(out_40));
  Register register_41 (.D(mixColumns3_coluna2), .Q(register_41_q));  // open: en, clk, clr
  Register register_42 (.D(mixColumns3_coluna3), .Q(register_42_q));  // open: en, clk, clr
  Register register_43 (.D(mixColumns3_coluna4), .Q(register_43_q));  // open: en, clk, clr
  Register register_44 (.D(mixColumns3_coluna1), .Q(register_44_q));  // open: en, clk, clr
  Register c_13 (.D(in_25), .Q(c_13_q));  // open: en, clk, clr
  Register c_14 (.D(in_26), .Q(c_14_q));  // open: en, clk, clr
  Register c_15 (.D(in_27), .Q(c_15_q));  // open: en, clk, clr
  Register c_16 (.D(in_28), .Q(c_16_q));  // open: en, clk, clr
  addRoundKey addroundkey_13 (.in_1(register_44_q), .in_2(c_13_q), .out_3(out_41));
  addRoundKey addroundkey_14 (.in_1(register_41_q), .in_2(c_14_q), .out_3(out_42));
  addRoundKey addroundkey_15 (.in_1(register_42_q), .in_2(c_15_q), .out_3(out_43));
  addRoundKey addroundkey_16 (.in_1(register_43_q), .in_2(c_16_q), .out_3(out_44));

  // Notes on the sheet:
  //   subBytes
  //   subBytes
  //   subBytes
  //   subBytes
  //   subBytes
  //   subBytes
  //   subBytes
  //   subBytes
  //   shiftRows
  //   shiftRows
  //   shiftRows
  //   shiftRows
  //   shiftRows
  //   shiftRows
  //   1L2C
  //   1L3C
  //   1L4C
  //   2L1C
  //   2L2C
  //   2L3C
  //   2L4C
  //   3L1C
  //   3L2C
  //   3L3C
  //   3L4C
  //   4L1C
  //   4L2C
  //   4L3C
  //   4L4C
endmodule

module lastRound (
  input  [7:0] in_1,
  input  [7:0] chave,
  input  [7:0] in_3,
  input  [7:0] chave_2,
  input  [7:0] in_5,
  input  [7:0] chave_3,
  input  [7:0] in_7,
  input  [7:0] chave_4,
  input  [7:0] in_9,
  input  [7:0] chave_5,
  input  [7:0] in_11,
  input  [7:0] chave_6,
  input  [7:0] chave_7,
  input  [7:0] in_14,
  input  [7:0] chave_8,
  input  [7:0] in_16,
  input  [7:0] in_17,
  input  [7:0] in_18,
  input  [7:0] chave_9,
  input  [7:0] chave_10,
  input  [7:0] in_21,
  input  [7:0] chave_11,
  input  [7:0] chave_12,
  input  [7:0] in_24,
  input  [7:0] in_25,
  input  [7:0] in_26,
  input  [7:0] chave_13,
  input  [7:0] chave_14,
  input  [7:0] in_29,
  input  [7:0] chave_15,
  input  [7:0] chave_16,
  input  [7:0] in_32,
  output [7:0] out_33,
  output [7:0] out_34,
  output [7:0] out_35,
  output [7:0] out_36,
  output [7:0] out_37,
  output [7:0] out_38,
  output [7:0] out_39,
  output [7:0] out_40,
  output [7:0] out_41,
  output [7:0] out_42,
  output [7:0] out_43,
  output [7:0] out_44,
  output [7:0] out_45,
  output [7:0] out_46,
  output [7:0] out_47,
  output [7:0] out_48
);

  wire undriven;
  wire [7:0] c_2_q, c_3_q, c_4_q, c_5_q, c_6_q, c_7_q, c_8_q, c_9_q, c_10_q, c_11_q, c_12_q, c_13_q, c_14_q,
       c_15_q, c_16_q, c_q, register_1_q, register_2_q, register_3_q, register_4_q, register_5_q,
       register_6_q, register_7_q, register_8_q, register_9_q, register_10_q, register_11_q, register_12_q,
       register_13_q, register_14_q, register_15_q, register_16_q, register_17_q, register_18_q,
       register_19_q, register_20_q, register_21_q, register_22_q, register_23_q, register_24_q,
       register_25_q, register_26_q, register_27_q, register_28_q, register_29_q, register_30_q,
       register_31_q, register_32_q, register_33_q, register_34_q, register_35_q, register_36_q,
       register_37_q, register_38_q, register_39_q, register_40_q, register_41_q, register_42_q,
       register_43_q, register_44_q, rom_1_data, rom_2_data, rom_3_data, rom_4_data, rom_5_data, rom_6_data,
       rom_7_data, rom_8_data, rom_9_data, rom_10_data, rom_11_data, rom_12_data, rom_13_data, rom_14_data,
       rom_15_data, rom_16_data, shiftrows2_1_out_5, shiftrows2_1_out_6, shiftrows2_1_out_7,
       shiftrows2_1_out_8, shiftrows3_1_out_5, shiftrows3_1_out_6, shiftrows3_1_out_7, shiftrows3_1_out_8,
       shiftrows4_1_out_5, shiftrows4_1_out_6, shiftrows4_1_out_7, shiftrows4_1_out_8;

  ROM rom_1 (.addr(in_24), .data(rom_1_data));  // open: sel
  ROM rom_2 (.addr(in_25), .data(rom_2_data));  // open: sel
  ROM rom_3 (.addr(in_26), .data(rom_3_data));  // open: sel
  ROM rom_4 (.addr(in_29), .data(rom_4_data));  // open: sel
  ROM rom_5 (.addr(in_1), .data(rom_5_data));  // open: sel
  ROM rom_6 (.addr(in_3), .data(rom_6_data));  // open: sel
  ROM rom_7 (.addr(in_5), .data(rom_7_data));  // open: sel
  Register register_1 (.D(rom_8_data), .Q(register_1_q));  // open: en, clk, clr
  ROM rom_8 (.addr(in_7), .data(rom_8_data));  // open: sel
  Register register_2 (.D(rom_9_data), .Q(register_2_q));  // open: en, clk, clr
  ROM rom_9 (.addr(in_9), .data(rom_9_data));  // open: sel
  Register register_3 (.D(rom_10_data), .Q(register_3_q));  // open: en, clk, clr
  ROM rom_10 (.addr(in_11), .data(rom_10_data));  // open: sel
  Register register_4 (.D(rom_11_data), .Q(register_4_q));  // open: en, clk, clr
  ROM rom_11 (.addr(in_14), .data(rom_11_data));  // open: sel
  Register register_5 (.D(rom_12_data), .Q(register_5_q));  // open: en, clk, clr
  ROM rom_12 (.addr(in_16), .data(rom_12_data));  // open: sel
  Register register_6 (.D(rom_13_data), .Q(register_6_q));  // open: en, clk, clr
  ROM rom_13 (.addr(in_17), .data(rom_13_data));  // open: sel
  ROM rom_14 (.addr(in_18), .data(rom_14_data));  // open: sel
  Register register_7 (.D(rom_14_data), .Q(register_7_q));  // open: en, clk, clr
  ROM rom_15 (.addr(in_21), .data(rom_15_data));  // open: sel
  Register register_8 (.D(rom_15_data), .Q(register_8_q));  // open: en, clk, clr
  Register register_9 (.D(rom_1_data), .Q(register_9_q));  // open: en, clk, clr
  Register register_10 (.D(rom_2_data), .Q(register_10_q));  // open: en, clk, clr
  Register register_11 (.D(rom_3_data), .Q(register_11_q));  // open: en, clk, clr
  Register register_12 (.D(rom_4_data), .Q(register_12_q));  // open: en, clk, clr
  ROM rom_16 (.addr(in_32), .data(rom_16_data));  // open: sel
  Register register_13 (.D(rom_16_data), .Q(register_13_q));  // open: en, clk, clr
  Register register_14 (.D(rom_5_data), .Q(register_14_q));  // open: en, clk, clr
  Register register_15 (.D(rom_6_data), .Q(register_15_q));  // open: en, clk, clr
  Register register_16 (.D(rom_7_data), .Q(register_16_q));  // open: en, clk, clr
  shiftRows3 shiftrows3_1 (
    .in_1(register_6_q), .in_2(register_7_q), .in_3(register_8_q), .in_4(register_9_q),
    .out_5(shiftrows3_1_out_5), .out_6(shiftrows3_1_out_6), .out_7(shiftrows3_1_out_7),
    .out_8(shiftrows3_1_out_8));
  shiftRows2 shiftrows2_1 (
    .in_1(register_2_q), .in_2(register_3_q), .in_3(register_4_q), .in_4(register_5_q),
    .out_5(shiftrows2_1_out_5), .out_6(shiftrows2_1_out_6), .out_7(shiftrows2_1_out_7),
    .out_8(shiftrows2_1_out_8));
  shiftRows4 shiftrows4_1 (
    .in_1(register_10_q), .in_2(register_11_q), .in_3(register_12_q), .in_4(register_13_q),
    .out_5(shiftrows4_1_out_5), .out_6(shiftrows4_1_out_6), .out_7(shiftrows4_1_out_7),
    .out_8(shiftrows4_1_out_8));
  Register register_17 (.D(register_16_q), .Q(register_17_q));  // open: en, clk, clr
  Register register_18 (.D(shiftrows2_1_out_5), .Q(register_18_q));  // open: en, clk, clr
  Register register_19 (.D(shiftrows2_1_out_6), .Q(register_19_q));  // open: en, clk, clr
  Register register_20 (.D(shiftrows2_1_out_7), .Q(register_20_q));  // open: en, clk, clr
  Register register_21 (.D(shiftrows2_1_out_8), .Q(register_21_q));  // open: en, clk, clr
  Register register_22 (.D(shiftrows3_1_out_5), .Q(register_22_q));  // open: en, clk, clr
  Register register_23 (.D(shiftrows3_1_out_6), .Q(register_23_q));  // open: en, clk, clr
  Register register_24 (.D(shiftrows3_1_out_7), .Q(register_24_q));  // open: en, clk, clr
  Register register_25 (.D(shiftrows3_1_out_8), .Q(register_25_q));  // open: en, clk, clr
  Register register_26 (.D(shiftrows4_1_out_5), .Q(register_26_q));  // open: en, clk, clr
  Register register_27 (.D(shiftrows4_1_out_6), .Q(register_27_q));  // open: en, clk, clr
  Register register_28 (.D(shiftrows4_1_out_7), .Q(register_28_q));  // open: en, clk, clr
  Register register_29 (.D(shiftrows4_1_out_8), .Q(register_29_q));  // open: en, clk, clr
  Register register_30 (.D(register_15_q), .Q(register_30_q));  // open: en, clk, clr
  Register c (.D(chave_3), .Q(c_q));  // open: en, clk, clr
  Register register_31 (.D(register_1_q), .Q(register_31_q));  // open: en, clk, clr
  Register c_2 (.D(chave_4), .Q(c_2_q));  // open: en, clk, clr
  Register register_32 (.D(register_14_q), .Q(register_32_q));  // open: en, clk, clr
  Register c_3 (.D(chave), .Q(c_3_q));  // open: en, clk, clr
  addRoundKey addRoundKey (.in_1(register_30_q), .in_2(c_4_q), .out_3(out_34));
  Register c_4 (.D(chave_2), .Q(c_4_q));  // open: en, clk, clr
  addRoundKey addRoundKey_2 (.in_1(register_17_q), .in_2(c_q), .out_3(out_35));
  addRoundKey addRoundKey_3 (.in_1(register_31_q), .in_2(c_2_q), .out_3(out_36));
  Register register_33 (.D(register_25_q), .Q(register_33_q));  // open: en, clk, clr
  Register c_5 (.D(chave_12), .Q(c_5_q));  // open: en, clk, clr
  Register register_34 (.D(register_29_q), .Q(register_34_q));  // open: en, clk, clr
  Register c_6 (.D(chave_16), .Q(c_6_q));  // open: en, clk, clr
  addRoundKey addRoundKey_4 (.in_1(register_32_q), .in_2(c_3_q), .out_3(out_33));
  Register register_35 (.D(register_18_q), .Q(register_35_q));  // open: en, clk, clr
  Register c_7 (.D(chave_5), .Q(c_7_q));  // open: en, clk, clr
  Register register_36 (.D(register_22_q), .Q(register_36_q));  // open: en, clk, clr
  Register c_8 (.D(chave_9), .Q(c_8_q));  // open: en, clk, clr
  addRoundKey addRoundKey_5 (.in_1(register_33_q), .in_2(c_5_q), .out_3(out_44));
  Register register_37 (.D(register_26_q), .Q(register_37_q));  // open: en, clk, clr
  Register c_9 (.D(chave_13), .Q(c_9_q));  // open: en, clk, clr
  Register register_38 (.D(register_28_q), .Q(register_38_q));  // open: en, clk, clr
  Register c_10 (.D(chave_15), .Q(c_10_q));  // open: en, clk, clr
  addRoundKey addRoundKey_6 (.in_1(register_34_q), .in_2(c_6_q), .out_3(out_48));
  addRoundKey addRoundKey_7 (.in_1(register_35_q), .in_2(c_7_q), .out_3(out_37));
  Register register_39 (.D(register_21_q), .Q(register_39_q));  // open: en, clk, clr
  Register c_11 (.D(chave_8), .Q(c_11_q));  // open: en, clk, clr
  addRoundKey addRoundKey_8 (.in_1(register_36_q), .in_2(c_8_q), .out_3(out_41));
  Register register_40 (.D(register_23_q), .Q(register_40_q));  // open: en, clk, clr
  Register c_12 (.D(chave_10), .Q(c_12_q));  // open: en, clk, clr
  Register register_41 (.D(register_24_q), .Q(register_41_q));  // open: en, clk, clr
  Register c_13 (.D(chave_11), .Q(c_13_q));  // open: en, clk, clr
  addRoundKey addRoundKey_9 (.in_1(register_37_q), .in_2(c_9_q), .out_3(out_45));
  Register register_42 (.D(register_27_q), .Q(register_42_q));  // open: en, clk, clr
  Register c_14 (.D(chave_14), .Q(c_14_q), .clk(undriven), .clr(undriven));  // open: en
  addRoundKey addRoundKey_10 (.in_1(register_38_q), .in_2(c_10_q), .out_3(out_47));
  Register register_43 (.D(register_19_q), .Q(register_43_q));  // open: en, clk, clr
  Register c_15 (.D(chave_6), .Q(c_15_q));  // open: en, clk, clr
  Register register_44 (.D(register_20_q), .Q(register_44_q));  // open: en, clk, clr
  Register c_16 (.D(chave_7), .Q(c_16_q));  // open: en, clk, clr
  addRoundKey addRoundKey_11 (.in_1(register_39_q), .in_2(c_11_q), .out_3(out_40));
  addRoundKey addRoundKey_12 (.in_1(register_40_q), .in_2(c_12_q), .out_3(out_42));
  addRoundKey addRoundKey_13 (.in_1(register_41_q), .in_2(c_13_q), .out_3(out_43));
  addRoundKey addRoundKey_14 (.in_1(register_42_q), .in_2(c_14_q), .out_3(out_46));
  addRoundKey addRoundKey_15 (.in_1(register_43_q), .in_2(c_15_q), .out_3(out_38));
  addRoundKey addRoundKey_16 (.in_1(register_44_q), .in_2(c_16_q), .out_3(out_39));

  // Notes on the sheet:
  //   subBytes
  //   subBytes
  //   subBytes
  //   subBytes
  //   subBytes
  //   subBytes
  //   subBytes
  //   subBytes
  //   subBytes
  //   subBytes
  //   subBytes
  //   subBytes
  //   subBytes
  //   subBytes
  //   subBytes
  //   subBytes
  //   shiftRows
  //   shiftRows
  //   shiftRows
  //   shiftRows
  //   shiftRows
  //   1L2C
  //   1L4C
  //   shiftRows
  //   1L3C
  //   2L1C
  //   2L2C
  //   2L3C
  //   2L4C
  //   3L1C
  //   3L2C
  //   3L3C
  //   3L4C
  //   4L1C
  //   4L2C
  //   4L3C
  //   4L4C
endmodule
